# Fritzing sketch BREADBOARD (saved by Fritzing 0.9.3b)
breadboards: 1
perfboards: 5

parts:
  Bauteil1 = Arduino Uno (Rev3)
  U5 = 74HC4052 [package=dil16]
  U9 = 74HC4052 [package=dil16]
  U10 = 74HC4052 [package=dil16]
  U11 = 74HC4052 [package=dil16]
  U13 = 74HC4052 [package=dil16]
  U14 = 74HC4052 [package=dil16]
  U8 = 74HC4052 [package=dil16]
  U1 = 74HC4052 [package=dil16]
  R2 = Rotary Potentiometer (Small) [maximum_resistance=100kΩ package=THT]
  R3 = Rotary Potentiometer (Small) [maximum_resistance=100kΩ package=THT]
  J1 = BANANA_CONN [package=banana_conn]  # not connected
  J2 = BANANA_CONN [package=banana_conn]  # not connected
  R4 = Slide Potentiometer [maximum_resistance=100kΩ]
  R6 = Rotary Potentiometer (Small) [maximum_resistance=100kΩ package=THT]
  J3 = BANANA_CONN [package=banana_conn]  # not connected
  J4 = BANANA_CONN [package=banana_conn]  # not connected
  R7 = Rotary Potentiometer (Small) [maximum_resistance=100kΩ package=THT]
  J5 = BANANA_CONN [package=banana_conn]  # not connected
  J6 = BANANA_CONN [package=banana_conn]  # not connected
  R9 = Rotary Potentiometer (Small) [maximum_resistance=100kΩ package=THT]
  R10 = Rotary Potentiometer (Small) [maximum_resistance=100kΩ package=THT]
  J7 = BANANA_CONN [package=banana_conn]  # not connected
  J8 = BANANA_CONN [package=banana_conn]  # not connected
  S4 = Toggle Switch [package=THT]
  J9 = BANANA_CONN [package=banana_conn]  # not connected
  J10 = BANANA_CONN [package=banana_conn]  # not connected
  R11 = Rotary Potentiometer (Small) [maximum_resistance=100kΩ package=THT]
  R12 = Rotary Potentiometer (Small) [maximum_resistance=100kΩ package=THT]
  J11 = BANANA_CONN [package=banana_conn]  # not connected
  J12 = BANANA_CONN [package=banana_conn]  # not connected
  J13 = BANANA_CONN [package=banana_conn]  # not connected
  J14 = BANANA_CONN [package=banana_conn]  # not connected
  R13 = Resistor [tolerance=±5% resistance=220 package="1206 [SMD]"]
  R14 = Resistor [tolerance=±5% resistance=220 package="1206 [SMD]"]
  R15 = Resistor [tolerance=±5% resistance=220 package="0805 [SMD]"]
  R16 = Resistor [tolerance=±5% resistance=220 package="1206 [SMD]"]
  R17 = Resistor [tolerance=±5% resistance=220 package="1206 [SMD]"]
  R18 = Resistor [tolerance=±5% resistance=220 package="0805 [SMD]"]
  J15 = BANANA_CONN [package=banana_conn]
  J16 = BANANA_CONN [package=banana_conn]
  R20 = Resistor [tolerance=±5% resistance=220 package="1206 [SMD]"]
  R21 = Resistor [tolerance=±5% resistance=220 package="1206 [SMD]"]
  R22 = Resistor [tolerance=±5% resistance=220 package="0805 [SMD]"]
  R24 = Resistor [tolerance=±5% resistance=220 package="1206 [SMD]"]
  R25 = Resistor [tolerance=±5% resistance=220 package="0805 [SMD]"]
  R26 = Resistor [tolerance=±5% resistance=220 package="0805 [SMD]"]

nets:
  N1: Bauteil1.A0, U1.Y
  N2: Bauteil1.A3, U5.X3
  N3: Bauteil1.A4/SDA, U5.A
  N4: Bauteil1.D8, U10.X3, U14.X3, U8.X3
  N5: Bauteil1.D9_PWM, U10.A, U14.A, U8.A
  N6: Bauteil1.D10_PWM/SS, U10.B, U14.B, U8.B
  N7: Bauteil1.D11_PWM/MOSI, U9.X3, U11.X3, U1.X3
  N8: Bauteil1.D12/MISO, U9.A, U11.A, U1.A
  N9: Bauteil1.D13/SCK, U9.B, U11.B, U1.B
  N10: Bauteil1.D1/TX, U9.Y
  N11: Bauteil1.D3_PWM, U13.Y
  N12: Bauteil1.D4, U11.Y
  N13: Bauteil1.D5_PWM, U13.X3
  N14: Bauteil1.D6_PWM, U13.A
  N15: Bauteil1.D7, U13.B
  N16: U5.Y, U13.X
  GND: U5.INH, U5.VEE, U5.GND, U9.INH, U9.VEE, U9.GND, U10.INH, U10.VEE, U10.GND, U11.INH, U11.VEE, U11.GND, U13.INH, U13.VEE, U13.GND, U14.INH, U14.VEE, U14.GND, U8.INH, U8.VEE, U8.GND, U1.INH, U1.VEE, U1.GND, R13.Pin_0, R14.Pin_1, R15.Pin_0, R16.Pin_0, R17.Pin_0, R18.Pin_0, R20.Pin_0, R21.Pin_0, R22.Pin_0, R24.Pin_1, R25.Pin_0, R26.Pin_0
  VCC: U5.VCC, U9.VCC, U10.VCC, U11.VCC, U13.VCC, U14.VCC, U8.VCC, U1.VCC
  N17: U9.Y2, U9.Y3, U9.Y1, R20.Pin_1
  N18: U9.X0, U9.X1, U9.X2, R26.Pin_1
  N19: U9.X, U8.Y
  N20: U10.Y2, U10.Y3, U10.Y1, R14.Pin_0
  N21: U10.Y, U1.X
  N22: U11.Y0, U11.Y2, U11.Y3, U11.Y1, R16.Pin_1
  N23: U11.X0, R15.Pin_1
  N24: U11.X, U14.Y
  N25: U13.Y2, U13.Y3, U13.Y1, R24.Pin_0
  N26: U13.X0, U13.X1, U13.X2, R25.Pin_1
  N27: U14.Y0, U14.Y2, U14.Y3, U14.Y1, R17.Pin_1
  N28: U14.X0, R18.Pin_1
  N29: U8.Y0, U8.Y2, U8.Y3, U8.Y1, R21.Pin_1
  N30: U8.X0, U8.X, U8.X1, U8.X2, R22.Pin_1
  N31: U1.Y0, U1.Y2, U1.Y1, R13.Pin_1
  N32: U1.Y3, R11.wiper
  N33: U1.X0, R2.wiper
  N34: U1.X1, R4.wiper
  N35: U1.X2, R3.wiper
  N36: R2.leg1, R3.leg1, R6.leg1, R7.leg1, R10.leg1, R11.leg1, J15.1
  N37: R2.leg2, R3.leg2, R4.leg1, R11.leg2
  N38: R6.leg2, R7.leg2, S4.L2, J16.1
  N39: R9.leg2, R10.leg2, R12.leg2

notes:
  A
  B
  D
  C
  A1
  B1
  D1
  C1
  VCO1
  VCO2
  OUTPUTS
  INPUTS
  CV
